// Logisim project main.circ as structural Verilog
module ALU (
  input  a,
  input  [1:0] c,
  input  [15:0] in_3,
  input  [15:0] in_4,
  output FLAG,
  output [15:0] OUTPUT
);

  wire adder_1_cout, and_2_out, subtractor_1_bout;
  wire [15:0] adder_1_out, and_1_out, divider_1_out, divider_1_rem, multiplexer_1_out, multiplexer_2_out,
       multiplier_1_cout, multiplier_1_out, negator_1_out, or_1_out, subtractor_1_out, xor_1_out;

  Adder #(.width(16)) adder_1 (.a(in_3), .b(in_4), .out(adder_1_out), .cout(adder_1_cout));  // open: cin
  Subtractor #(.width(16)) subtractor_1 (
    .a(in_3), .b(in_4), .out(subtractor_1_out), .bout(subtractor_1_bout));  // open: bin
  Multiplier #(.width(16)) multiplier_1 (
    .a(in_3), .b(in_4), .out(multiplier_1_out), .cout(multiplier_1_cout));  // open: cin
  Divider #(.width(16)) divider_1 (.a(in_3), .b(in_4), .out(divider_1_out), .rem(divider_1_rem));  // open: upper
  assign and_1_out = in_3 & in_4;  // AND_Gate and_1, 16 bits wide
  assign or_1_out = in_3 | in_4;  // OR_Gate or_1, 16 bits wide
  assign xor_1_out = in_3 ^ in_4;  // XOR_Gate xor_1, 16 bits wide
  Negator #(.width(16)) negator_1 (.in(in_3), .out(negator_1_out));
  Multiplexer #(.select(2), .width(16), .enable("false")) multiplexer_1 (
    .in0(adder_1_out), .in1(subtractor_1_out), .in2(multiplier_1_out), .in3(divider_1_out),
    .out(multiplexer_1_out), .sel(c));
  Multiplexer #(.select(2), .width(16), .enable("false")) multiplexer_2 (
    .in0(and_1_out), .in1(or_1_out), .in2(xor_1_out), .in3(negator_1_out), .out(multiplexer_2_out), .sel(c));
  Multiplexer #(.width(16), .enable("false")) multiplexer_3 (
    .in0(multiplexer_1_out), .in1(multiplexer_2_out), .out(OUTPUT), .sel(a));
  and and_2 (and_2_out, multiplier_1_cout[0], multiplier_1_cout[1], multiplier_1_cout[2], multiplier_1_cout[3], multiplier_1_cout[4], multiplier_1_cout[5], multiplier_1_cout[6], multiplier_1_cout[7], multiplier_1_cout[8], multiplier_1_cout[9], multiplier_1_cout[10], multiplier_1_cout[11], multiplier_1_cout[12], multiplier_1_cout[13], multiplier_1_cout[14], multiplier_1_cout[15], divider_1_rem[0], divider_1_rem[1], divider_1_rem[2], divider_1_rem[3], divider_1_rem[4], divider_1_rem[5], divider_1_rem[6], divider_1_rem[7], divider_1_rem[8], divider_1_rem[9], divider_1_rem[10], divider_1_rem[11], divider_1_rem[12], divider_1_rem[13], divider_1_rem[14], divider_1_rem[15]);
  nor nor_1 (FLAG, adder_1_cout, subtractor_1_bout, and_2_out);

  // Notes on the sheet:
  //   b
  //   A
  //   TR
  //   ADDER
  //   DIVIDER
  //   AND
  //   OR
  //   XOR
  //   SUBTRACTOR 
  //   MULTIPLIER
  //   NEGATION
endmodule
